# Fritzing sketch Roomba-schematic-diagram (saved by Fritzing 1.0.1rc)

parts:
  Part1 = Arduino Uno (Rev3)  # not connected
  Part2 = Rotoshield - Motor driver shield for Arduino
  VCC1 = Battery block 9V
  S1 = Toggle Switch [package=THT]
  HC-SR04_Sensor_1 = HC-SR04 Ultrasonic Distance Sensor
  M1 = fc-51 [package=THT]
  M2 = fc-51 [package=THT]
  M4 = DC Motor [voltage_(max)=6V voltage_(min)=3V]
  M3 = DC Motor [voltage_(max)=6V voltage_(min)=3V]

nets:
  N1: Part2.A_IN_1, M1.pin1
  N2: Part2.A_IN_2, HC-SR04_Sensor_1.TRIG
  N3: Part2.A_IN_3, HC-SR04_Sensor_1.ECHO
  N4: Part2.A_IN_4, M2.pin1
  +5V: Part2.+5V, HC-SR04_Sensor_1.VCC, M1.pin3, M2.pin3
  GND: Part2.GND, VCC1.-, HC-SR04_Sensor_1.GND, M1.pin2, M2.pin2
  N5: Part2.M1-2, M3.pin_1
  N6: Part2.M1-1, M3.pin_2
  N7: Part2.M2-2, M4.pin_1
  N8: Part2.M2-1, M4.pin_2
  N9: Part2.VCC, S1.L2
